// Logisim project ALU_Group32.circ as structural Verilog: 19 circuits, main circuit main
module main (
  output halt,
  output [8:0] counter,
  output [3:0] op,
  output [15:0] a,
  output [15:0] b,
  output [15:0] oracle,
  output [15:0] result,
  output err_oracle,
  output error,
  output ok,
  output start_delimiter
);

  wire and_1_out, and_2_out, clock_1_out, comparator_1_eq, comparator_2_eq;

  Clock clock_1 (.out(clock_1_out));
  Counter #(.width(9), .max('h1ff), .trigger("falling")) counter_1 (
    .Q(counter), .carry(halt), .clk(clock_1_out));  // open: load, D, count, clr
  RAM #(.addrWidth(12), .dataWidth(4), .bus("separate")) ram_1 (
    .addr({counter, 3'b000}), .data(op), .ld(1'b1));  // open: din, str, sel, clk, clr
  RAM #(.addrWidth(12), .dataWidth(16), .bus("separate")) ram_2 (
    .addr({counter, 3'b001}), .data(a), .ld(1'b1));  // open: din, str, sel, clk, clr
  RAM #(.addrWidth(12), .dataWidth(16), .bus("separate")) ram_3 (
    .addr({counter, 3'b010}), .data(b), .ld(1'b1));  // open: din, str, sel, clk, clr
  RAM #(.addrWidth(12), .dataWidth(16), .bus("separate")) ram_4 (
    .addr({counter, 3'b011}), .data(oracle), .ld(1'b1));  // open: din, str, sel, clk, clr
  RAM #(.addrWidth(12), .dataWidth(1), .bus("separate")) ram_5 (
    .addr({counter, 3'b100}), .data(err_oracle), .ld(1'b1));  // open: din, str, sel, clk, clr
  RAM #(.addrWidth(12), .dataWidth(1), .bus("separate")) ram_6 (
    .addr({counter, 3'b101}), .data(start_delimiter), .ld(1'b1));  // open: din, str, sel, clk, clr
  _16_bit_ALU u_16_bit_alu_1 (.ALU_code(op), .a(a), .b(b), .overflow(error), .result(result));
  Comparator #(.width(1), .mode("unsigned")) comparator_1 (
    .a(error), .b(err_oracle), .eq(comparator_1_eq));  // open: gt, lt
  Comparator #(.width(16)) comparator_2 (.a(result), .b(oracle), .eq(comparator_2_eq));  // open: gt, lt
  and and_1 (and_1_out, comparator_1_eq, error);
  and and_2 (and_2_out, comparator_2_eq, comparator_1_eq, ~error);  // AND_Gate
  or or_1 (ok, and_1_out, and_2_out);

  // Notes on the sheet:
  //   You must complete the circuit '12-bit ALU' instead.
  //   DO NOT EDIT THIS CIRCUIT!
endmodule

module _16_bit_ALU (
  input  [3:0] ALU_code,
  input  [15:0] a,
  input  [15:0] b,
  output [15:0] result,
  output overflow
);

  wire add_1_overflow, inv_1_overflow, sla_1_overflow, sub_1_overflow;
  wire [15:0] add_1_output, and_1_output, eq_1_output, gt_1_output, inv_1_output, lt_1_output, neq_1_output,
       noop_1_output, not_1_out_2, or_1_output, sla_1_output, sll_1_output, sra_1_output, srl_1_output,
       sub_1_output, zero_1_out_1;

  zero zero_1 (.out_1(zero_1_out_1));
  Not not_1 (.a(a), .out_2(not_1_out_2));
  And and_1 (.a(a), .b(b), .Output(and_1_output));
  Or or_1 (.a(a), .b(b), .Output(or_1_output));
  add add_1 (.a(a), .b(b), .Output(add_1_output), .Overflow(add_1_overflow));
  sub sub_1 (.a(a), .b(b), .Output(sub_1_output), .Overflow(sub_1_overflow));
  lt lt_1 (.a(a), .b(b), .Output(lt_1_output));
  gt gt_1 (.a(a), .b(b), .Output(gt_1_output));
  eq eq_1 (.a(a), .b(b), .Output(eq_1_output));
  neq neq_1 (.a(a), .b(b), .Output(neq_1_output));
  inv inv_1 (.a(a), .Output(inv_1_output), .Overflow(inv_1_overflow));
  sll sll_1 (.a(a), .Output(sll_1_output));
  srl srl_1 (.a(a), .Output(srl_1_output));
  sla sla_1 (.a(a), .Output(sla_1_output), .Overflow(sla_1_overflow));
  sra sra_1 (.a(a), .Output(sra_1_output));
  noop noop_1 (.a(a), .Output(noop_1_output));
  Multiplexer #(.select(4), .width(16)) multiplexer_1 (
    .in0(zero_1_out_1), .in1(not_1_out_2), .in2(and_1_output), .in3(or_1_output), .in4(add_1_output),
    .in5(sub_1_output), .in6(lt_1_output), .in7(gt_1_output), .in8(eq_1_output), .in9(neq_1_output),
    .in10(inv_1_output), .in11(sll_1_output), .in12(srl_1_output), .in13(sla_1_output), .in14(sra_1_output),
    .in15(noop_1_output), .out(result), .sel(ALU_code));  // open: en
  Multiplexer #(.select(4)) multiplexer_2 (
    .in0(1'b0), .in1(1'b0), .in2(1'b0), .in3(1'b0), .in4(add_1_overflow), .in5(sub_1_overflow), .in6(1'b0),
    .in7(1'b0), .in8(1'b0), .in9(1'b0), .in10(inv_1_overflow), .in11(1'b0), .in12(1'b0),
    .in13(sla_1_overflow), .in14(1'b0), .in15(1'b0), .out(overflow), .sel(ALU_code));  // open: en

  // Notes on the sheet:
  //   This circuit is used as a block in the main circuit, and its layout must remain unchanged. The circuit called "main" should be the main circuit of this file.
  //   Do not change the circuit appearance.
  //   DO NOT CHANGE THE INPUTS AND OUTPUTS OF THIS CIRCUIT!
  //   Do not add/remove inputs or outputs. Do not even change their location or orientation.
endmodule

module zero (
  output [15:0] out_1
);


  assign out_1 = {16{1'b0}};
endmodule

module Not (
  input  [15:0] a,
  output [15:0] out_2
);

  assign out_2 = ~a;  // NOT_Gate not_1, 16 bits wide
endmodule

module And (
  input  [15:0] a,
  input  [15:0] b,
  output [15:0] Output
);

  assign Output = a & b;  // AND_Gate and_1, 16 bits wide
endmodule

module Or (
  input  [15:0] a,
  input  [15:0] b,
  output [15:0] Output
);

  assign Output = a | b;  // OR_Gate or_1, 16 bits wide
endmodule

module add (
  input  [15:0] a,
  input  [15:0] b,
  output [15:0] Output,
  output Overflow
);

  Oef_3_16bit_carry_lookahead_adder oef_3_16bit_carry_lookahead_adder_1 (
    .CarryIn(1'b0), .a(a), .b(b), .Sum(Output), .Overflow(Overflow));
endmodule

module sub (
  input  [15:0] a,
  input  [15:0] b,
  output [15:0] Output,
  output Overflow
);

  wire [15:0] not_1_out;

  assign not_1_out = ~b;  // NOT_Gate not_1, 16 bits wide
  Oef_3_16bit_carry_lookahead_adder oef_3_16bit_carry_lookahead_adder_1 (
    .CarryIn(1'b1), .a(a), .b(not_1_out), .Sum(Output), .Overflow(Overflow));
endmodule

module sll (
  input  [15:0] a,
  output [15:0] Output
);


  assign Output = {a[14:0], 1'b0};
endmodule

module eq (
  input  [15:0] a,
  input  [15:0] b,
  output [15:0] Output
);

  wire and_1_out, xnor_1_out, xnor_2_out, xnor_3_out, xnor_4_out, xnor_5_out, xnor_6_out, xnor_7_out,
       xnor_8_out, xnor_9_out, xnor_10_out, xnor_11_out, xnor_12_out, xnor_13_out, xnor_14_out, xnor_15_out,
       xnor_16_out;

  xnor xnor_1 (xnor_1_out, a[0], b[0]);
  xnor xnor_2 (xnor_2_out, a[1], b[1]);
  xnor xnor_3 (xnor_3_out, a[2], b[2]);
  xnor xnor_4 (xnor_4_out, a[3], b[3]);
  xnor xnor_5 (xnor_5_out, a[4], b[4]);
  xnor xnor_6 (xnor_6_out, a[5], b[5]);
  xnor xnor_7 (xnor_7_out, a[6], b[6]);
  xnor xnor_8 (xnor_8_out, a[7], b[7]);
  xnor xnor_9 (xnor_9_out, a[8], b[8]);
  xnor xnor_10 (xnor_10_out, a[9], b[9]);
  xnor xnor_11 (xnor_11_out, a[10], b[10]);
  xnor xnor_12 (xnor_12_out, a[11], b[11]);
  xnor xnor_13 (xnor_13_out, a[12], b[12]);
  xnor xnor_14 (xnor_14_out, a[13], b[13]);
  xnor xnor_15 (xnor_15_out, a[14], b[14]);
  xnor xnor_16 (xnor_16_out, a[15], b[15]);
  and and_1 (and_1_out, xnor_1_out, xnor_2_out, xnor_3_out, xnor_4_out, xnor_5_out, xnor_6_out, xnor_7_out, xnor_8_out, xnor_9_out, xnor_10_out, xnor_11_out, xnor_12_out, xnor_13_out, xnor_14_out, xnor_15_out, xnor_16_out);
  assign Output = {{15{1'b0}}, and_1_out};  // Bit_Extender bit_extender_1
endmodule

module noop (
  input  [15:0] a,
  output [15:0] Output
);


  assign Output = a;
endmodule

module sla (
  input  [15:0] a,
  output [15:0] Output,
  output Overflow
);

  add add_1 (.a(a), .b(a), .Output(Output), .Overflow(Overflow));
endmodule

module srl (
  input  [15:0] a,
  output [15:0] Output
);


  assign Output = {1'b0, a[15:1]};
endmodule

module sra (
  input  [15:0] a,
  output [15:0] Output
);

  and and_1 (Output[15], a[15], 1'b1);

  assign Output[14:0] = a[15:1];
endmodule

module neq (
  input  [15:0] a,
  input  [15:0] b,
  output [15:0] Output
);

  wire and_1_out, not_1_out, xnor_1_out, xnor_2_out, xnor_3_out, xnor_4_out, xnor_5_out, xnor_6_out,
       xnor_7_out, xnor_8_out, xnor_9_out, xnor_10_out, xnor_11_out, xnor_12_out, xnor_13_out, xnor_14_out,
       xnor_15_out, xnor_16_out;

  xnor xnor_1 (xnor_1_out, a[0], b[0]);
  xnor xnor_2 (xnor_2_out, a[1], b[1]);
  xnor xnor_3 (xnor_3_out, a[2], b[2]);
  xnor xnor_4 (xnor_4_out, a[3], b[3]);
  xnor xnor_5 (xnor_5_out, a[4], b[4]);
  xnor xnor_6 (xnor_6_out, a[5], b[5]);
  xnor xnor_7 (xnor_7_out, a[6], b[6]);
  xnor xnor_8 (xnor_8_out, a[7], b[7]);
  xnor xnor_9 (xnor_9_out, a[8], b[8]);
  xnor xnor_10 (xnor_10_out, a[9], b[9]);
  xnor xnor_11 (xnor_11_out, a[10], b[10]);
  xnor xnor_12 (xnor_12_out, a[11], b[11]);
  xnor xnor_13 (xnor_13_out, a[12], b[12]);
  xnor xnor_14 (xnor_14_out, a[13], b[13]);
  xnor xnor_15 (xnor_15_out, a[14], b[14]);
  xnor xnor_16 (xnor_16_out, a[15], b[15]);
  not not_1 (not_1_out, and_1_out);
  and and_1 (and_1_out, xnor_1_out, xnor_2_out, xnor_3_out, xnor_4_out, xnor_5_out, xnor_6_out, xnor_7_out, xnor_8_out, xnor_9_out, xnor_10_out, xnor_11_out, xnor_12_out, xnor_13_out, xnor_14_out, xnor_15_out, xnor_16_out);
  assign Output = {{15{1'b0}}, not_1_out};  // Bit_Extender bit_extender_1
endmodule

module lt (
  input  [15:0] a,
  input  [15:0] b,
  output [15:0] Output
);

  wire n16_bit_carry_lookahead_set_1_set;
  wire [15:0] not_1_out;

  assign not_1_out = ~b;  // NOT_Gate not_1, 16 bits wide
  _16_bit_carry_lookahead___set u_16_bit_carry_lookahead_set_1 (
    .CarryIn(1'b1), .a(a), .b(not_1_out), .Set(n16_bit_carry_lookahead_set_1_set));  // open: Sum, Overflow
  assign Output = {{15{1'b0}}, n16_bit_carry_lookahead_set_1_set};  // Bit_Extender bit_extender_1
endmodule

module inv (
  input  [15:0] a,
  output [15:0] Output,
  output Overflow
);

  wire [15:0] not_1_out;

  assign not_1_out = ~a;  // NOT_Gate not_1, 16 bits wide
  sub sub_1 (.a(not_1_out), .b({16{1'b1}}), .Output(Output), .Overflow(Overflow));
endmodule

module _16_bit_carry_lookahead___set (
  input  CarryIn,
  input  [15:0] a,
  input  [15:0] b,
  output [15:0] Sum,
  output Overflow,
  output Set
);

  wire and_1_out, and_2_out, and_3_out, and_4_out, and_5_out, and_6_out, n4_bit_cla_1_g0, n4_bit_cla_1_p0,
       n4_bit_cla_2_g0, n4_bit_cla_2_p0, n4_bit_cla_3_g0, n4_bit_cla_3_p0, or_1_out, or_2_out, or_3_out;

  _4_bit_cla u_4_bit_cla_1 (
    .CarryIn(CarryIn), .a(a[3:0]), .b(b[3:0]), .Sum(Sum[3:0]), .P0(n4_bit_cla_1_p0), .G0(n4_bit_cla_1_g0));  // open: Overflow
  _4_bit_cla u_4_bit_cla_2 (
    .CarryIn(or_1_out), .a(a[7:4]), .b(b[7:4]), .Sum(Sum[7:4]), .P0(n4_bit_cla_2_p0), .G0(n4_bit_cla_2_g0));  // open: Overflow
  _4_bit_cla u_4_bit_cla_3 (
    .CarryIn(or_2_out), .a(a[11:8]), .b(b[11:8]), .Sum(Sum[11:8]), .P0(n4_bit_cla_3_p0), .G0(n4_bit_cla_3_g0));  // open: Overflow
  _4_bit_cla u_4_bit_cla_4 (
    .CarryIn(or_3_out), .a(a[15:12]), .b(b[15:12]), .Overflow(Overflow), .Sum(Sum[15:12]));  // open: P0, G0
  and and_1 (and_1_out, CarryIn, n4_bit_cla_1_p0);
  and and_2 (and_2_out, n4_bit_cla_2_p0, n4_bit_cla_1_g0);
  and and_3 (and_3_out, n4_bit_cla_2_p0, n4_bit_cla_1_p0, CarryIn);
  and and_4 (and_4_out, n4_bit_cla_3_p0, n4_bit_cla_2_g0);
  and and_5 (and_5_out, n4_bit_cla_3_p0, n4_bit_cla_2_p0, n4_bit_cla_1_g0);
  and and_6 (and_6_out, n4_bit_cla_3_p0, n4_bit_cla_2_p0, n4_bit_cla_1_p0, CarryIn);
  or or_1 (or_1_out, and_1_out, n4_bit_cla_1_g0);
  or or_2 (or_2_out, and_2_out, and_3_out, n4_bit_cla_2_g0);
  or or_3 (or_3_out, and_4_out, and_5_out, and_6_out, n4_bit_cla_3_g0);
  xor xor_1 (Set, Sum[15], Overflow);
endmodule

module gt (
  input  [15:0] a,
  input  [15:0] b,
  output [15:0] Output
);

  wire n16_bit_carry_lookahead_set_1_set;
  wire [15:0] not_1_out;

  assign not_1_out = ~a;  // NOT_Gate not_1, 16 bits wide
  _16_bit_carry_lookahead___set u_16_bit_carry_lookahead_set_1 (
    .CarryIn(1'b1), .a(not_1_out), .b(b), .Set(n16_bit_carry_lookahead_set_1_set));  // open: Sum, Overflow
  assign Output = {{15{1'b0}}, n16_bit_carry_lookahead_set_1_set};  // Bit_Extender bit_extender_1
endmodule
