// Logisim project SD_Group32.circ as structural Verilog: 13 circuits, main circuit main
module main (
  output [15:0] pc,
  output [15:0] r0,
  output [15:0] r1,
  output [15:0] r2,
  output [15:0] r3,
  output [15:0] r4,
  output [15:0] r5,
  output [15:0] r6,
  output [15:0] r7,
  output halt
);

  wire and_1_out, and_2_out, bit_extender_1_out, clock_1_out, control_unit_1_branch, control_unit_1_for_halt,
       control_unit_1_for_jump, control_unit_1_inc_dec, control_unit_1_j_jal, control_unit_1_jump_register,
       control_unit_1_mem_op, control_unit_1_sw, control_unit_1_unisgned_imm_yes_no,
       control_unit_1_write_on_off, halt_1_halt, n16_bit_alu_1_overflow, reset_out;
  wire [2:0] control_unit_1_rd, control_unit_1_rs, control_unit_1_rt, multiplexer_2_out;
  wire [3:0] control_unit_1_alu_code;
  wire [15:0] control_unit_1_immediate_opp, multiplexer_1_out, multiplexer_3_out, multiplexer_4_out,
       multiplexer_5_out, multiplexer_6_out, multiplexer_7_out, n16_bit_alu_1_result, n16_bit_pc_1_pc_1,
       ram_1_data, ram_2_data, register_file_1_s, register_file_1_t;

  or or_1 (halt, n16_bit_alu_1_overflow, halt_1_halt, control_unit_1_for_halt);
  Halt halt_1 (.instruction(ram_1_data), .clock(clock_1_out), .reset(reset_out), .halt(halt_1_halt));
  Clock clock_1 (.out(clock_1_out));
  Button reset (.out(reset_out));
  and and_1 (and_1_out, ~halt, clock_1_out);  // AND_Gate
  Bit_Extender #(.in_width(16), .out_width(1)) bit_extender_1 (.in(n16_bit_alu_1_result), .out(bit_extender_1_out));
  Multiplexer #(.width(16), .enable("false")) multiplexer_1 (
    .in0(control_unit_1_immediate_opp), .in1(n16_bit_alu_1_result), .out(multiplexer_1_out),
    .sel(control_unit_1_jump_register));
  and and_2 (and_2_out, bit_extender_1_out, control_unit_1_branch);
  _16_bit_pc u_16_bit_pc_1 (
    .branch_value(multiplexer_1_out), .branch_relative(and_2_out), .branch_abolute(control_unit_1_for_jump),
    .instruction_adress(pc), .C(and_1_out), .reset(reset_out), .pc_1(n16_bit_pc_1_pc_1));
  RAM #(.addrWidth(16), .dataWidth(16)) ram_1 (.addr(pc), .data(ram_1_data));  // open: sel, clk, ld, clr
  control_unit control_unit_1 (
    .Instruction(ram_1_data), .alu_code(control_unit_1_alu_code), .rd(control_unit_1_rd),
    .rs(control_unit_1_rs), .sw(control_unit_1_sw), .rt(control_unit_1_rt),
    .Immediate_opp(control_unit_1_immediate_opp), .mem_op(control_unit_1_mem_op),
    .unisgned_imm_yes_no(control_unit_1_unisgned_imm_yes_no), .inc_dec(control_unit_1_inc_dec),
    .j_jal(control_unit_1_j_jal), .for_jump(control_unit_1_for_jump),
    .write_on_off(control_unit_1_write_on_off), .branch(control_unit_1_branch),
    .jump_register(control_unit_1_jump_register), .for_halt(control_unit_1_for_halt));  // open: lui_yes_no, beq_blt
  Multiplexer #(.width(3), .enable("false")) multiplexer_2 (
    .in0(control_unit_1_rt), .in1(control_unit_1_rd), .out(multiplexer_2_out),
    .sel(control_unit_1_unisgned_imm_yes_no));
  register_file register_file_1 (
    .S(register_file_1_s), .T(register_file_1_t), .r0(r0), .r1(r1), .r2(r2), .r3(r3), .r4(r4), .r5(r5),
    .r6(r6), .r7(r7), .write(control_unit_1_write_on_off), .rs(control_unit_1_rs), .rt(multiplexer_2_out),
    .C(and_1_out), .reset(reset_out), .rd(control_unit_1_rd), .Data(multiplexer_3_out));
  Multiplexer #(.width(16), .enable("false")) multiplexer_3 (
    .in0(multiplexer_7_out), .in1(n16_bit_pc_1_pc_1), .out(multiplexer_3_out), .sel(control_unit_1_j_jal));
  Multiplexer #(.width(16), .enable("false")) multiplexer_4 (
    .in0(register_file_1_t), .in1(control_unit_1_immediate_opp), .out(multiplexer_4_out),
    .sel(control_unit_1_unisgned_imm_yes_no));
  Multiplexer #(.width(16), .enable("false")) multiplexer_5 (
    .in0(multiplexer_4_out), .in1(register_file_1_t), .out(multiplexer_5_out), .sel(control_unit_1_branch));
  _16_bit_ALU u_16_bit_alu_1 (
    .ALU_code(control_unit_1_alu_code), .a(register_file_1_s), .b(multiplexer_6_out),
    .overflow(n16_bit_alu_1_overflow), .result(n16_bit_alu_1_result));
  Multiplexer #(.width(16), .enable("false")) multiplexer_6 (
    .in0(multiplexer_5_out), .in1(16'h1), .out(multiplexer_6_out), .sel(control_unit_1_inc_dec));
  Multiplexer #(.width(16), .enable("false")) multiplexer_7 (
    .in0(n16_bit_alu_1_result), .in1(ram_2_data), .out(multiplexer_7_out), .sel(control_unit_1_mem_op));
  RAM #(.addrWidth(16), .dataWidth(16), .bus("separate")) ram_2 (
    .addr(n16_bit_alu_1_result), .din(register_file_1_t), .data(ram_2_data), .str(control_unit_1_sw),
    .clk(and_1_out), .ld(1'b1));  // open: sel, clr

  // Notes on the sheet:
  //   current instruction
  //   clock signal
  //   reset button
  //   DO NOT CHANGE THE INPUTS AND OUTPUTS OF THIS CIRCUIT! Do not add/remove inputs or outputs. Do not even change their location or orientation.
endmodule

module Halt (
  input  [15:0] instruction,
  input  clock,
  input  reset,
  output halt
);

  wire and_1_out, comparator_1_eq, comparator_2_gt, counter_1_carry, or_1_out, or_2_out;
  wire [11:0] counter_1_q;

  Comparator #(.width(16), .mode("unsigned")) comparator_1 (
    .a(instruction), .b({16{1'b0}}), .eq(comparator_1_eq));  // open: gt, lt
  Counter #(.width(12), .max('hfff), .trigger("falling")) counter_1 (
    .Q(counter_1_q), .carry(counter_1_carry), .clk(clock), .clr(reset));  // open: load, D, count
  or or_1 (or_1_out, comparator_1_eq, counter_1_carry);
  Comparator #(.width(12), .mode("unsigned")) comparator_2 (
    .a(counter_1_q), .b({12{1'b0}}), .gt(comparator_2_gt));  // open: eq, lt
  or or_2 (or_2_out, halt, and_1_out);
  and and_1 (and_1_out, or_1_out, comparator_2_gt);
  Register #(.width(1)) register_1 (.D(or_2_out), .Q(halt), .clk(clock), .clr(reset));  // open: en

  // Notes on the sheet:
  //   halt becomes and stays asserted if the instruction is 0000 (not in the first clock cycle) or the end of the counter is reached (2^12)
endmodule

module _16_bit_pc (
  input  C,
  input  reset,
  input  [15:0] branch_value,
  input  branch_relative,
  input  branch_abolute,
  output [15:0] pc_1,
  output [15:0] instruction_adress
);

  wire nand_1_out;
  wire [15:0] adder_2_out, multiplexer_1_out, multiplexer_2_out;

  nand nand_1 (nand_1_out, branch_relative, branch_abolute);
  Adder #(.width(16)) adder_1 (.a(16'h1), .b(instruction_adress), .out(pc_1));  // open: cin, cout
  Adder #(.width(16)) adder_2 (.a(pc_1), .b(branch_value), .out(adder_2_out));  // open: cin, cout
  Multiplexer #(.width(16), .enable("false")) multiplexer_1 (
    .in0(pc_1), .in1(adder_2_out), .out(multiplexer_1_out), .sel(branch_relative));
  Multiplexer #(.width(16), .enable("false")) multiplexer_2 (
    .in0(multiplexer_1_out), .in1(branch_value), .out(multiplexer_2_out), .sel(branch_abolute));
  _16_bit_register u_16_bit_register_1 (
    .D(multiplexer_2_out), .write(nand_1_out), .C(C), .reset(reset), .Q(instruction_adress));
endmodule

module ls_lw (
  input  [15:0] Instruction,
  output [2:0] rd,
  output [2:0] rs,
  output [15:0] signed_imm,
  output lw_sw,
  output sw
);

  wire not_1_out;

  not not_1 (not_1_out, Instruction[15]);
  and and_1 (lw_sw, not_1_out, Instruction[14], Instruction[13]);
  and and_2 (sw, lw_sw, Instruction[12]);
  assign signed_imm = {{10{Instruction[5]}}, Instruction[5:0]};  // Bit_Extender bit_extender_1

  assign rd = Instruction[11:9];
  assign rs = Instruction[8:6];
endmodule

module control_unit (
  input  [15:0] Instruction,
  output branch,
  output sw,
  output beq_blt,
  output lui_yes_no,
  output jump_register,
  output unisgned_imm_yes_no,
  output mem_op,
  output [3:0] alu_code,
  output [2:0] rd,
  output [2:0] rs,
  output [2:0] rt,
  output [15:0] Immediate_opp,
  output inc_dec,
  output for_jump,
  output j_jal,
  output write_on_off,
  output for_halt
);

  wire and_1_out, and_2_out, and_3_out, and_4_out, and_5_out, and_6_out, and_10_out, and_11_out, and_12_out,
       and_13_out, and_14_out, and_15_out, comparator_1_eq, comparator_2_eq, comparator_3_lt,
       jump_1_jump_or_jump_and_link, ls_lw_1_lw_sw, not_1_out, not_2_out, not_3_out, not_4_out, not_5_out,
       not_6_out, not_7_out, not_8_out, or_1_out, or_4_out, or_6_out, or_7_out, or_8_out, or_10_out,
       unsigned_imm_1_unsigned_yes_no;
  wire [2:0] binairy_1_rd, binairy_1_rs, binairy_1_rt, branch_1_rd, branch_1_rs, jump_register_1_rd,
       ls_lw_1_rd, ls_lw_1_rs, unary_1_rd, unary_1_rs, unsigned_imm_1_rd, unsigned_imm_1_rs;
  wire [3:0] binairy_1_alu_code, multiplexer_2_out, unary_1_alu_code, unsigned_imm_1_alu_code;
  wire [15:0] branch_1_immediate__signed, jump_1_target_address, jump_register_1_immediate__signed,
       ls_lw_1_signed_imm, unsigned_imm_1_unsigned_imm;

  not not_1 (not_1_out, Instruction[15]);
  and and_1 (and_1_out, not_1_out, not_2_out);
  not not_2 (not_2_out, Instruction[14]);
  not not_3 (not_3_out, Instruction[13]);
  not not_4 (not_4_out, Instruction[13]);
  not not_5 (not_5_out, Instruction[14]);
  not not_6 (not_6_out, Instruction[15]);
  not not_7 (not_7_out, Instruction[12]);
  Comparator #(.width(4)) comparator_1 (.a(alu_code), .b(4'b0100), .eq(comparator_1_eq));  // open: gt, lt
  Comparator #(.width(4)) comparator_2 (.a(alu_code), .b(4'b0101), .eq(comparator_2_eq));  // open: gt, lt
  and and_2 (and_2_out, Instruction[13], Instruction[14], Instruction[15]);
  and and_3 (and_3_out, not_3_out, Instruction[14], Instruction[15]);
  Comparator #(.width(3), .mode("unsigned")) comparator_3 (
    .a(Instruction[15:13]), .b(3'b011), .lt(comparator_3_lt));  // open: gt, eq
  and and_4 (and_4_out, not_4_out, not_5_out, Instruction[15]);
  and and_5 (and_5_out, Instruction[13], Instruction[14], not_6_out, not_7_out);
  and and_6 (and_6_out, Instruction[13], Instruction[14], Instruction[15], Instruction[12]);
  not not_8 (not_8_out, Instruction[15]);
  and and_7 (mem_op, not_8_out, Instruction[14], Instruction[13]);
  or or_1 (or_1_out, comparator_1_eq, comparator_2_eq);
  or or_2 (for_jump, and_2_out, and_3_out);
  or or_3 (write_on_off, comparator_3_lt, and_4_out, and_5_out, and_6_out);
  Multiplexer #(.select(3), .width(4), .enable("false")) multiplexer_1 (
    .in0(4'b0000), .in1(unary_1_alu_code), .in2(binairy_1_alu_code), .in3(4'b0100),
    .in4(unsigned_imm_1_alu_code), .in5(multiplexer_2_out), .in6(4'b0100), .in7(4'b0000), .out(alu_code),
    .sel(Instruction[15:13]));
  and and_8 (inc_dec, or_1_out, and_1_out);
  Multiplexer #(.width(4), .enable("false")) multiplexer_2 (
    .in0(4'b1000), .in1(4'b0111), .out(multiplexer_2_out), .sel(beq_blt));
  and and_9 (j_jal, jump_1_jump_or_jump_and_link, for_jump);
  Multiplexer #(.select(3), .width(3), .enable("false")) multiplexer_3 (
    .in0(unary_1_rd), .in1(unary_1_rd), .in2(binairy_1_rd), .in3(ls_lw_1_rd), .in4(unsigned_imm_1_rd),
    .in5(branch_1_rd), .in6(jump_register_1_rd), .in7(3'b111), .out(rd), .sel(Instruction[15:13]));
  and and_10 (and_10_out, ~Instruction[15], ~Instruction[14], ~Instruction[13]);  // AND_Gate
  Unary unary_1 (.Instruction(Instruction), .alu_code(unary_1_alu_code), .rd(unary_1_rd), .rs(unary_1_rs));
  Multiplexer #(.select(3), .width(3), .enable("false")) multiplexer_4 (
    .in0(3'b000), .in1(unary_1_rs), .in2(binairy_1_rs), .in3(ls_lw_1_rs), .in4(unsigned_imm_1_rs),
    .in5(branch_1_rs), .in6(jump_register_1_rd), .in7(3'b000), .out(rs), .sel(Instruction[15:13]));
  or or_4 (or_4_out, Instruction[12], Instruction[11], Instruction[10], Instruction[6], Instruction[5], Instruction[4], Instruction[3], Instruction[2], Instruction[1], Instruction[0]);
  and and_11 (and_11_out, and_10_out, or_4_out);
  Binairy binairy_1 (
    .Instruction(Instruction), .alu_code(binairy_1_alu_code), .rd(binairy_1_rd), .rs(binairy_1_rs),
    .rt(binairy_1_rt));
  and and_12 (and_12_out, ~Instruction[15], ~Instruction[14], Instruction[13]);  // AND_Gate
  ls_lw ls_lw_1 (
    .Instruction(Instruction), .lw_sw(ls_lw_1_lw_sw), .sw(sw), .rd(ls_lw_1_rd), .rs(ls_lw_1_rs),
    .signed_imm(ls_lw_1_signed_imm));
  Multiplexer #(.select(3), .width(3), .enable("false")) multiplexer_5 (
    .in0(3'b000), .in1(3'b000), .in2(binairy_1_rt), .in3(3'b000), .in4(3'b000), .in5(3'b000), .in6(3'b000),
    .in7(3'b000), .out(rt), .sel(Instruction[15:13]));
  and and_13 (and_13_out, and_12_out, or_7_out);
  or or_5 (for_halt, and_11_out, and_13_out, and_15_out);
  or or_6 (or_6_out, unsigned_imm_1_unsigned_yes_no, ls_lw_1_lw_sw);
  unsigned_imm unsigned_imm_1 (
    .Instruction(Instruction), .unsigned_yes_no(unsigned_imm_1_unsigned_yes_no), .rd(unsigned_imm_1_rd),
    .alu_code(unsigned_imm_1_alu_code), .unsigned_imm(unsigned_imm_1_unsigned_imm), .lui(lui_yes_no),
    .rs(unsigned_imm_1_rs));
  Multiplexer #(.select(3), .width(16), .enable("false")) multiplexer_6 (
    .in0({16{1'b0}}), .in1({16{1'b0}}), .in2({16{1'b0}}), .in3(ls_lw_1_signed_imm),
    .in4(unsigned_imm_1_unsigned_imm), .in5(branch_1_immediate__signed),
    .in6(jump_register_1_immediate__signed), .in7(jump_1_target_address), .out(Immediate_opp),
    .sel(Instruction[15:13]));
  or or_7 (or_7_out, Instruction[2], Instruction[1], Instruction[0]);
  and and_14 (and_14_out, Instruction[15], Instruction[14], ~Instruction[13]);  // AND_Gate
  branch branch_1 (
    .Instruction(Instruction), .immediate__signed(branch_1_immediate__signed), .beq_or_blt(beq_blt),
    .rd(branch_1_rd), .rs(branch_1_rs), .branch(branch));
  or or_8 (or_8_out, or_6_out, jump_register);
  or or_9 (unisgned_imm_yes_no, or_8_out, branch);
  or or_10 (or_10_out, Instruction[12], Instruction[11]);
  and and_15 (and_15_out, and_14_out, or_10_out);
  jump_register jump_register_1 (
    .Instruction(Instruction), .immediate__signed(jump_register_1_immediate__signed),
    .rd(jump_register_1_rd), .jump_register(jump_register));  // open: rs
  jump jump_1 (
    .Instruction(Instruction), .target_address(jump_1_target_address),
    .jump_or_jump_and_link(jump_1_jump_or_jump_and_link));
endmodule

module register_file (
  input  reset,
  input  write,
  input  [2:0] rs,
  input  [2:0] rt,
  input  C,
  input  [2:0] rd,
  input  [15:0] Data,
  output [15:0] S,
  output [15:0] T,
  output [15:0] r0,
  output [15:0] r1,
  output [15:0] r2,
  output [15:0] r3,
  output [15:0] r4,
  output [15:0] r5,
  output [15:0] r6,
  output [15:0] r7
);

  wire and_1_out, and_2_out, and_3_out, and_4_out, and_5_out, and_6_out, and_7_out, and_8_out,
       decoder_1_out0, decoder_1_out1, decoder_1_out2, decoder_1_out3, decoder_1_out4, decoder_1_out5,
       decoder_1_out6, decoder_1_out7;

  Decoder #(.select(3)) decoder_1 (
    .out0(decoder_1_out0), .out1(decoder_1_out1), .out2(decoder_1_out2), .out3(decoder_1_out3),
    .out4(decoder_1_out4), .out5(decoder_1_out5), .out6(decoder_1_out6), .out7(decoder_1_out7), .sel(rd));  // open: en
  and and_1 (and_1_out, write, decoder_1_out0);
  and and_2 (and_2_out, write, decoder_1_out1);
  and and_3 (and_3_out, write, decoder_1_out2);
  and and_4 (and_4_out, write, decoder_1_out3);
  and and_5 (and_5_out, write, decoder_1_out4);
  and and_6 (and_6_out, write, decoder_1_out5);
  and and_7 (and_7_out, write, decoder_1_out6);
  and and_8 (and_8_out, write, decoder_1_out7);
  _16_bit_register u_16_bit_register_1 (.D({16{1'b0}}), .write(and_1_out), .C(C), .reset(reset), .Q(r0));
  _16_bit_register u_16_bit_register_2 (.D(Data), .write(and_2_out), .C(C), .reset(reset), .Q(r1));
  _16_bit_register u_16_bit_register_3 (.D(Data), .write(and_3_out), .C(C), .reset(reset), .Q(r2));
  _16_bit_register u_16_bit_register_4 (.D(Data), .write(and_4_out), .C(C), .reset(reset), .Q(r3));
  _16_bit_register u_16_bit_register_5 (.D(Data), .write(and_5_out), .C(C), .reset(reset), .Q(r4));
  _16_bit_register u_16_bit_register_6 (.D(Data), .write(and_6_out), .C(C), .reset(reset), .Q(r5));
  _16_bit_register u_16_bit_register_7 (.D(Data), .write(and_7_out), .C(C), .reset(reset), .Q(r6));
  _16_bit_register u_16_bit_register_8 (.D(Data), .write(and_8_out), .C(C), .reset(reset), .Q(r7));
  Multiplexer #(.select(3), .width(16)) multiplexer_1 (
    .in0(r0), .in1(r1), .in2(r2), .in3(r3), .in4(r4), .in5(r5), .in6(r6), .in7(r7), .out(S), .sel(rs));  // open: en
  Multiplexer #(.select(3), .width(16)) multiplexer_2 (
    .in0(r0), .in1(r1), .in2(r2), .in3(r3), .in4(r4), .in5(r5), .in6(r6), .in7(r7), .out(T), .sel(rt));  // open: en
endmodule

module _16_bit_register (
  input  write,
  input  C,
  input  reset,
  input  [15:0] D,
  output [15:0] Q
);

  D_Flip_Flop #(.trigger("falling")) d_ff_1 (
    .clk(C), .D(D[0]), .Q(Q[0]), .en(write), .reset(reset));  // open: Qn, preset
  D_Flip_Flop #(.trigger("falling")) d_ff_2 (
    .clk(C), .D(D[1]), .Q(Q[1]), .en(write), .reset(reset));  // open: Qn, preset
  D_Flip_Flop #(.trigger("falling")) d_ff_3 (
    .clk(C), .D(D[2]), .Q(Q[2]), .en(write), .reset(reset));  // open: Qn, preset
  D_Flip_Flop #(.trigger("falling")) d_ff_4 (
    .clk(C), .D(D[3]), .Q(Q[3]), .en(write), .reset(reset));  // open: Qn, preset
  D_Flip_Flop #(.trigger("falling")) d_ff_5 (
    .clk(C), .D(D[4]), .Q(Q[4]), .en(write), .reset(reset));  // open: Qn, preset
  D_Flip_Flop #(.trigger("falling")) d_ff_6 (
    .clk(C), .D(D[5]), .Q(Q[5]), .en(write), .reset(reset));  // open: Qn, preset
  D_Flip_Flop #(.trigger("falling")) d_ff_7 (
    .clk(C), .D(D[6]), .Q(Q[6]), .en(write), .reset(reset));  // open: Qn, preset
  D_Flip_Flop #(.trigger("falling")) d_ff_8 (
    .clk(C), .D(D[7]), .Q(Q[7]), .en(write), .reset(reset));  // open: Qn, preset
  D_Flip_Flop #(.trigger("falling")) d_ff_9 (
    .clk(C), .D(D[8]), .Q(Q[8]), .en(write), .reset(reset));  // open: Qn, preset
  D_Flip_Flop #(.trigger("falling")) d_ff_10 (
    .clk(C), .D(D[9]), .Q(Q[9]), .en(write), .reset(reset));  // open: Qn, preset
  D_Flip_Flop #(.trigger("falling")) d_ff_11 (
    .clk(C), .D(D[10]), .Q(Q[10]), .en(write), .reset(reset));  // open: Qn, preset
  D_Flip_Flop #(.trigger("falling")) d_ff_12 (
    .clk(C), .D(D[11]), .Q(Q[11]), .en(write), .reset(reset));  // open: Qn, preset
  D_Flip_Flop #(.trigger("falling")) d_ff_13 (
    .clk(C), .D(D[12]), .Q(Q[12]), .en(write), .reset(reset));  // open: Qn, preset
  D_Flip_Flop #(.trigger("falling")) d_ff_14 (
    .clk(C), .D(D[13]), .Q(Q[13]), .en(write), .reset(reset));  // open: Qn, preset
  D_Flip_Flop #(.trigger("falling")) d_ff_15 (
    .clk(C), .D(D[14]), .Q(Q[14]), .en(write), .reset(reset));  // open: Qn, preset
  D_Flip_Flop #(.trigger("falling")) d_ff_16 (
    .clk(C), .D(D[15]), .Q(Q[15]), .en(write), .reset(reset));  // open: Qn, preset
endmodule

module Unary (
  input  [15:0] Instruction,
  output [3:0] alu_code,
  output [2:0] rd,
  output [2:0] rs
);


  assign alu_code = Instruction[12:9];
  assign rd = Instruction[8:6];
  assign rs = Instruction[5:3];
endmodule

module Binairy (
  input  [15:0] Instruction,
  output [3:0] alu_code,
  output [2:0] rd,
  output [2:0] rs,
  output [2:0] rt
);


  assign alu_code = Instruction[12:9];
  assign rd = Instruction[8:6];
  assign rs = Instruction[5:3];
  assign rt = Instruction[2:0];
endmodule

// lui
module unsigned_imm (
  input  [15:0] Instruction,
  output [2:0] rd,
  output [2:0] rs,
  output unsigned_yes_no,
  output [15:0] unsigned_imm,
  output lui,
  output [3:0] alu_code
);

  wire not_1_out, not_2_out, not_3_out;
  wire [15:0] bit_extender_1_out;

  not not_1 (not_1_out, Instruction[14]);
  not not_2 (not_2_out, Instruction[13]);
  and and_1 (unsigned_yes_no, Instruction[15], not_1_out, not_2_out);
  Multiplexer #(.width(3), .disabled(0), .enable("false")) multiplexer_1 (
    .in0(Instruction[10:8]), .in1(3'b000), .out(rs), .sel(lui));
  Multiplexer #(.select(2), .width(4), .enable("false")) multiplexer_2 (
    .in0(4'b0011), .in1(4'b0100), .in2(4'b0100), .in3(4'b0101), .out(alu_code), .sel(Instruction[12:11]));
  and u_lui (lui, Instruction[15], not_3_out, Instruction[11]);
  not not_3 (not_3_out, Instruction[12]);
  Multiplexer #(.width(16), .enable("false")) multiplexer_3 (
    .in0(bit_extender_1_out), .in1({Instruction[7:0], {8{1'b0}}}), .out(unsigned_imm), .sel(lui));
  assign bit_extender_1_out = {{8{1'b0}}, Instruction[7:0]};  // Bit_Extender bit_extender_1

  assign rd = Instruction[10:8];
endmodule

module branch (
  input  [15:0] Instruction,
  output [2:0] rd,
  output [2:0] rs,
  output [15:0] immediate__signed,
  output branch,
  output beq_or_blt
);

  wire not_1_out;

  not not_1 (not_1_out, Instruction[14]);
  and and_1 (branch, Instruction[15], not_1_out, Instruction[13]);
  and and_2 (beq_or_blt, branch, Instruction[12]);
  assign immediate__signed = {{10{Instruction[5]}}, Instruction[5:0]};  // Bit_Extender bit_extender_1

  assign rd = Instruction[11:9];
  assign rs = Instruction[8:6];
endmodule

module jump_register (
  input  [15:0] Instruction,
  output [2:0] rd,
  output [2:0] rs,
  output [15:0] immediate__signed,
  output jump_register
);

  wire not_1_out;

  not not_1 (not_1_out, Instruction[13]);
  and and_1 (jump_register, Instruction[15], Instruction[14], not_1_out);
  assign immediate__signed = {{8{Instruction[7]}}, Instruction[7:0]};  // Bit_Extender bit_extender_1

  assign rd = Instruction[10:8];
  assign rs = Instruction[10:8];
endmodule

module jump (
  input  [15:0] Instruction,
  output [15:0] target_address,
  output jump_or_jump_and_link
);

  assign target_address = {{4{1'b0}}, Instruction[11:0]};  // Bit_Extender bit_extender_1

  assign jump_or_jump_and_link = Instruction[12];
endmodule
