// Logisim project project 2new .circ as structural Verilog: 5 circuits, main circuit Oef 3 16bit carry lookahead adder
module Oef_3_16bit_carry_lookahead_adder (
  input  CarryIn,
  input  [15:0] a,
  input  [15:0] b,
  output [15:0] Sum,
  output Overflow
);

  wire and_1_out, and_2_out, and_3_out, and_4_out, and_5_out, and_6_out, n4_bit_cla_1_g0, n4_bit_cla_1_p0,
       n4_bit_cla_2_g0, n4_bit_cla_2_p0, n4_bit_cla_3_g0, n4_bit_cla_3_p0, or_1_out, or_2_out, or_3_out;

  _4_bit_cla u_4_bit_cla_1 (
    .CarryIn(CarryIn), .a(a[3:0]), .b(b[3:0]), .Sum(Sum[3:0]), .P0(n4_bit_cla_1_p0), .G0(n4_bit_cla_1_g0));  // open: Overflow
  _4_bit_cla u_4_bit_cla_2 (
    .CarryIn(or_1_out), .a(a[7:4]), .b(b[7:4]), .Sum(Sum[7:4]), .P0(n4_bit_cla_2_p0), .G0(n4_bit_cla_2_g0));  // open: Overflow
  _4_bit_cla u_4_bit_cla_3 (
    .CarryIn(or_2_out), .a(a[11:8]), .b(b[11:8]), .Sum(Sum[11:8]), .P0(n4_bit_cla_3_p0), .G0(n4_bit_cla_3_g0));  // open: Overflow
  _4_bit_cla u_4_bit_cla_4 (
    .CarryIn(or_3_out), .a(a[15:12]), .b(b[15:12]), .Overflow(Overflow), .Sum(Sum[15:12]));  // open: P0, G0
  and and_1 (and_1_out, CarryIn, n4_bit_cla_1_p0);
  and and_2 (and_2_out, n4_bit_cla_2_p0, n4_bit_cla_1_g0);
  and and_3 (and_3_out, n4_bit_cla_2_p0, n4_bit_cla_1_p0, CarryIn);
  and and_4 (and_4_out, n4_bit_cla_3_p0, n4_bit_cla_2_g0);
  and and_5 (and_5_out, n4_bit_cla_3_p0, n4_bit_cla_2_p0, n4_bit_cla_1_g0);
  and and_6 (and_6_out, n4_bit_cla_3_p0, n4_bit_cla_2_p0, n4_bit_cla_1_p0, CarryIn);
  or or_1 (or_1_out, and_1_out, n4_bit_cla_1_g0);
  or or_2 (or_2_out, and_2_out, and_3_out, n4_bit_cla_2_g0);
  or or_3 (or_3_out, and_4_out, and_5_out, and_6_out, n4_bit_cla_3_g0);
endmodule

module _4_bit_cla (
  input  CarryIn,
  input  [3:0] a,
  input  [3:0] b,
  output [3:0] Sum,
  output Overflow,
  output P0,
  output G0
);

  wire and_1_out, and_2_out, and_3_out, and_4_out, and_5_out, and_6_out, and_7_out, and_8_out, and_9_out,
       and_10_out, and_11_out, and_12_out, and_13_out, and_15_out, and_16_out, and_17_out, or_1_out,
       or_2_out, or_3_out, or_4_out, or_5_out, or_6_out, or_7_out, or_8_out, p2p1g0_out;

  or or_1 (or_1_out, a[0], b[0]);
  and and_1 (and_1_out, a[0], b[0]);
  or or_2 (or_2_out, a[1], b[1]);
  and and_2 (and_2_out, a[1], b[1]);
  or or_3 (or_3_out, a[2], b[2]);
  and and_3 (and_3_out, a[2], b[2]);
  or or_4 (or_4_out, a[3], b[3]);
  and and_4 (and_4_out, a[3], b[3]);
  and and_5 (and_5_out, CarryIn, or_1_out);
  and and_6 (and_6_out, or_2_out, and_1_out);
  and and_7 (and_7_out, or_2_out, or_1_out, CarryIn);
  and and_8 (and_8_out, or_3_out, and_2_out);
  and p2p1g0 (p2p1g0_out, or_3_out, or_3_out, or_2_out, and_1_out);
  and and_9 (and_9_out, or_3_out, or_2_out, or_1_out, CarryIn);
  and and_10 (and_10_out, or_4_out, and_3_out);
  and and_11 (and_11_out, or_4_out, or_3_out, and_2_out);
  and and_12 (and_12_out, or_4_out, or_3_out, or_2_out, and_1_out);
  and and_13 (and_13_out, or_4_out, or_3_out, or_2_out, or_1_out, CarryIn);
  and and_14 (P0, or_1_out, or_2_out, or_3_out, or_4_out);
  and and_15 (and_15_out, or_4_out, and_3_out);
  and and_16 (and_16_out, or_4_out, or_3_out, and_2_out);
  and and_17 (and_17_out, or_4_out, or_3_out, or_2_out, and_1_out);
  or or_5 (or_5_out, and_5_out, and_1_out);
  or or_6 (or_6_out, and_6_out, and_7_out, and_2_out);
  or or_7 (or_7_out, and_8_out, p2p1g0_out, and_9_out, and_3_out);
  or or_8 (or_8_out, and_10_out, and_11_out, and_12_out, and_13_out, and_4_out);
  or or_9 (G0, and_15_out, and_16_out, and_17_out, and_4_out);
  Oef_1_1bit_full_adder oef_1_1bit_full_adder_1 (
    .a(a[0]), .b(b[0]), .CarryIn(CarryIn), .Sum(Sum[0]));  // open: CarryOut
  Oef_1_1bit_full_adder oef_1_1bit_full_adder_2 (
    .a(a[1]), .b(b[1]), .CarryIn(or_5_out), .Sum(Sum[1]));  // open: CarryOut
  Oef_1_1bit_full_adder oef_1_1bit_full_adder_3 (
    .a(a[2]), .b(b[2]), .CarryIn(or_6_out), .Sum(Sum[2]));  // open: CarryOut
  Oef_1_1bit_full_adder oef_1_1bit_full_adder_4 (
    .a(a[3]), .b(b[3]), .CarryIn(or_7_out), .Sum(Sum[3]));  // open: CarryOut
  xor xor_1 (Overflow, or_7_out, or_8_out);

  // Notes on the sheet:
  //   p0
  //   g0
  //   p1
  //   g1
  //   p2
  //   g2
  //   p3
  //   g3
  //   p1g0
  //   p2g1
  //   p3g2
  //   p0c0
  //   p1p0c0
  //   p2p1p0c0
  //   p3p2g1
  //   p3p2p1g0
  //   p3p2p1p0c0
  //   p0
  //   g0 + p0c0
  //   g1 +p1g0+p1p0c0
  //   g2 + p2g1+p2p1g0+p2p1p0c0
  //   g3+p3g2+p3p2g1+p3p2p1pg0+p3p2p1p0c0
endmodule

module Comparison (
  input  [15:0] a,
  input  [15:0] b,
  input  CarryIn,
  output [15:0] Sum,
  output Overflow,
  output [15:0] Sum_2,
  output Overflow_2
);

  // Probe on a
  // Probe on b
  Oef_3_16bit_carry_lookahead_adder oef_3_16bit_carry_lookahead_adder_1 (
    .CarryIn(CarryIn), .a(a), .b(b), .Sum(Sum), .Overflow(Overflow));
  Oef_2_16bit_ripple_carry_adder oef_2_16bit_ripple_carry_adder_1 (
    .A(a), .B(b), .in_3(CarryIn), .Sum(Sum_2), .Overflow(Overflow_2));
  // Probe on Sum
  // Probe on Sum_2
endmodule

module Oef_1_1bit_full_adder (
  input  a,
  input  b,
  input  CarryIn,
  output CarryOut,
  output Sum
);

  wire and_1_out, and_2_out, and_3_out, and_4_out, and_5_out, and_6_out, and_7_out, not_1_out, not_2_out,
       not_3_out;

  not not_1 (not_1_out, a);
  not not_2 (not_2_out, b);
  not not_3 (not_3_out, CarryIn);
  and and_1 (and_1_out, not_1_out, b, CarryIn);
  and and_2 (and_2_out, a, not_2_out, CarryIn);
  and and_3 (and_3_out, a, b, not_3_out);
  and and_4 (and_4_out, a, b, CarryIn);
  and and_5 (and_5_out, not_1_out, not_2_out, CarryIn);
  and and_6 (and_6_out, not_1_out, b, not_3_out);
  and and_7 (and_7_out, a, not_2_out, not_3_out);
  or or_1 (CarryOut, and_4_out, and_3_out, and_2_out, and_1_out);
  or or_2 (Sum, and_7_out, and_6_out, and_5_out, and_4_out);

  // Notes on the sheet:
  //   1-Bit Full Adder
endmodule

module Oef_2_16bit_ripple_carry_adder (
  input  [15:0] A,
  input  [15:0] B,
  input  in_3,
  output [15:0] Sum,
  output Overflow
);

  wire oef_1_1bit_full_adder_1_carryout, oef_1_1bit_full_adder_2_carryout, oef_1_1bit_full_adder_3_carryout,
       oef_1_1bit_full_adder_4_carryout, oef_1_1bit_full_adder_5_carryout, oef_1_1bit_full_adder_6_carryout,
       oef_1_1bit_full_adder_7_carryout, oef_1_1bit_full_adder_8_carryout, oef_1_1bit_full_adder_9_carryout,
       oef_1_1bit_full_adder_10_carryout, oef_1_1bit_full_adder_11_carryout,
       oef_1_1bit_full_adder_12_carryout, oef_1_1bit_full_adder_13_carryout,
       oef_1_1bit_full_adder_14_carryout, oef_1_1bit_full_adder_15_carryout,
       oef_1_1bit_full_adder_16_carryout;

  Oef_1_1bit_full_adder oef_1_1bit_full_adder_1 (
    .a(A[0]), .b(B[0]), .CarryIn(in_3), .CarryOut(oef_1_1bit_full_adder_1_carryout), .Sum(Sum[0]));
  Oef_1_1bit_full_adder oef_1_1bit_full_adder_2 (
    .a(A[1]), .b(B[1]), .CarryIn(oef_1_1bit_full_adder_1_carryout),
    .CarryOut(oef_1_1bit_full_adder_2_carryout), .Sum(Sum[1]));
  Oef_1_1bit_full_adder oef_1_1bit_full_adder_3 (
    .a(A[9]), .b(B[9]), .CarryIn(oef_1_1bit_full_adder_16_carryout),
    .CarryOut(oef_1_1bit_full_adder_3_carryout), .Sum(Sum[9]));
  Oef_1_1bit_full_adder oef_1_1bit_full_adder_4 (
    .a(A[2]), .b(B[2]), .CarryIn(oef_1_1bit_full_adder_2_carryout),
    .CarryOut(oef_1_1bit_full_adder_4_carryout), .Sum(Sum[2]));
  Oef_1_1bit_full_adder oef_1_1bit_full_adder_5 (
    .a(A[10]), .b(B[10]), .CarryIn(oef_1_1bit_full_adder_3_carryout),
    .CarryOut(oef_1_1bit_full_adder_5_carryout), .Sum(Sum[10]));
  Oef_1_1bit_full_adder oef_1_1bit_full_adder_6 (
    .a(A[11]), .b(B[11]), .CarryIn(oef_1_1bit_full_adder_5_carryout),
    .CarryOut(oef_1_1bit_full_adder_6_carryout), .Sum(Sum[11]));
  Oef_1_1bit_full_adder oef_1_1bit_full_adder_7 (
    .a(A[3]), .b(B[3]), .CarryIn(oef_1_1bit_full_adder_4_carryout),
    .CarryOut(oef_1_1bit_full_adder_7_carryout), .Sum(Sum[3]));
  Oef_1_1bit_full_adder oef_1_1bit_full_adder_8 (
    .a(A[12]), .b(B[12]), .CarryIn(oef_1_1bit_full_adder_6_carryout),
    .CarryOut(oef_1_1bit_full_adder_8_carryout), .Sum(Sum[12]));
  Oef_1_1bit_full_adder oef_1_1bit_full_adder_9 (
    .a(A[4]), .b(B[4]), .CarryIn(oef_1_1bit_full_adder_7_carryout),
    .CarryOut(oef_1_1bit_full_adder_9_carryout), .Sum(Sum[4]));
  Oef_1_1bit_full_adder oef_1_1bit_full_adder_10 (
    .a(A[13]), .b(B[13]), .CarryIn(oef_1_1bit_full_adder_8_carryout),
    .CarryOut(oef_1_1bit_full_adder_10_carryout), .Sum(Sum[13]));
  Oef_1_1bit_full_adder oef_1_1bit_full_adder_11 (
    .a(A[5]), .b(B[5]), .CarryIn(oef_1_1bit_full_adder_9_carryout),
    .CarryOut(oef_1_1bit_full_adder_11_carryout), .Sum(Sum[5]));
  Oef_1_1bit_full_adder oef_1_1bit_full_adder_12 (
    .a(A[6]), .b(B[6]), .CarryIn(oef_1_1bit_full_adder_11_carryout),
    .CarryOut(oef_1_1bit_full_adder_12_carryout), .Sum(Sum[6]));
  Oef_1_1bit_full_adder oef_1_1bit_full_adder_13 (
    .a(A[14]), .b(B[14]), .CarryIn(oef_1_1bit_full_adder_10_carryout),
    .CarryOut(oef_1_1bit_full_adder_13_carryout), .Sum(Sum[14]));
  Oef_1_1bit_full_adder oef_1_1bit_full_adder_14 (
    .a(A[7]), .b(B[7]), .CarryIn(oef_1_1bit_full_adder_12_carryout),
    .CarryOut(oef_1_1bit_full_adder_14_carryout), .Sum(Sum[7]));
  Oef_1_1bit_full_adder oef_1_1bit_full_adder_15 (
    .a(A[15]), .b(B[15]), .CarryIn(oef_1_1bit_full_adder_13_carryout),
    .CarryOut(oef_1_1bit_full_adder_15_carryout), .Sum(Sum[15]));
  Oef_1_1bit_full_adder oef_1_1bit_full_adder_16 (
    .a(A[8]), .b(B[8]), .CarryIn(oef_1_1bit_full_adder_14_carryout),
    .CarryOut(oef_1_1bit_full_adder_16_carryout), .Sum(Sum[8]));
  xor xor_1 (Overflow, oef_1_1bit_full_adder_15_carryout, oef_1_1bit_full_adder_13_carryout);
endmodule
